# Fritzing sketch schwurbler360_apm_MCP23017 (saved by Fritzing 0.9.5d)
breadboards: 2

parts:
  Pro_Micro1 = SparkFun Pro Micro
  IC1 = MCP23017 I2C I/O Expander
  RE1 = Rotary Encoder [package=THT]
  ENCODER1 = Rotary Encoder with Knob
  RE2 = Rotary Encoder [package=THT]
  RE3 = Rotary Encoder [package=THT]
  RE4 = Rotary Encoder [package=THT]
  RE5 = Rotary Encoder [package=THT]
  RE6 = Rotary Encoder [package=THT]
  RE7 = Rotary Encoder [package=THT]
  RE8 = Rotary Encoder [package=THT]
  R1 = Resistor [tolerance=±5% resistance=10k package="0805 [SMD]"]
  R2 = Resistor [tolerance=±5% resistance=10k package="0805 [SMD]"]
  R3 = Resistor [tolerance=±5% resistance=10k package="0805 [SMD]"]
  R4 = Resistor [tolerance=±5% resistance=10k package="0805 [SMD]"]
  R5 = Resistor [tolerance=±5% resistance=10k package="0805 [SMD]"]
  R6 = Resistor [tolerance=±5% resistance=10k package="0805 [SMD]"]
  R7 = Resistor [tolerance=±5% resistance=10k package="0805 [SMD]"]
  R8 = Resistor [tolerance=±5% resistance=10k package="0805 [SMD]"]
  R9 = Resistor [tolerance=±5% resistance=10k package="0805 [SMD]"]
  R10 = Resistor [tolerance=±5% resistance=10k package="0805 [SMD]"]
  R11 = Resistor [tolerance=±5% resistance=10k package="0805 [SMD]"]
  R12 = Resistor [tolerance=±5% resistance=10k package="0805 [SMD]"]
  R13 = Resistor [tolerance=±5% resistance=10k package="0805 [SMD]"]
  R14 = Resistor [tolerance=±5% resistance=10k package="0805 [SMD]"]
  R15 = Resistor [tolerance=±5% resistance=10k package="0805 [SMD]"]
  R16 = Resistor [tolerance=±5% resistance=10k package="0805 [SMD]"]
  R17 = Resistor [tolerance=±5% resistance=10k package="0805 [SMD]"]
  R19 = Resistor [tolerance=±5% resistance=10k package="0805 [SMD]"]
  S1 = Pushbutton [part_number=COM-09190 package="[THT]"]
  S2 = Pushbutton [part_number=COM-09190 package="[THT]"]
  S3 = Pushbutton [part_number=COM-09190 package="[THT]"]
  S4 = Pushbutton [part_number=COM-09190 package="[THT]"]
  S5 = Pushbutton [part_number=COM-09190 package="[THT]"]
  S6 = Pushbutton [part_number=COM-09190 package="[THT]"]
  S7 = Pushbutton [part_number=COM-09190 package="[THT]"]
  S8 = Pushbutton [part_number=COM-09190 package="[THT]"]

nets:
  GND: Pro_Micro1.GND, IC1.VSS, IC1.A0, IC1.A1, IC1.A2, RE1.EncoderPinC, ENCODER1.no_name_yet#2, ENCODER1.no_name_yet#5, RE2.EncoderPinC, RE3.EncoderPinC, RE4.EncoderPinC, RE5.EncoderPinC, RE6.EncoderPinC, RE7.EncoderPinC, RE8.EncoderPinC, S1.Pin_1, S1.Pin_2, S3.Pin_1, S3.Pin_2, S4.Pin_1, S4.Pin_2, S5.Pin_1, S5.Pin_2, S6.Pin_1, S6.Pin_2, S7.Pin_1, S7.Pin_2, S8.Pin_1, S8.Pin_2
  N1: Pro_Micro1.2, IC1.SDA
  N2: Pro_Micro1.3, Pro_Micro1.4, IC1.SCL
  N3: Pro_Micro1.6, S6.Pin_3, S6.Pin_4
  N4: Pro_Micro1.7, S5.Pin_3, S5.Pin_4
  N5: Pro_Micro1.8, ENCODER1.no_name_yet#4
  N6: Pro_Micro1.9, IC1.INTA
  N7: Pro_Micro1.10, ENCODER1.no_name_yet#3, R19.Pin_1
  N8: Pro_Micro1.16, ENCODER1.no_name_yet#1, R17.Pin_1
  N9: Pro_Micro1.14, S7.Pin_3, S7.Pin_4
  N10: Pro_Micro1.15, S8.Pin_3, S8.Pin_4
  VCC: Pro_Micro1.VCC, IC1.VDD, IC1.RESET, R1.Pin_0, R2.Pin_0, R3.Pin_0, R4.Pin_0, R5.Pin_0, R6.Pin_0, R7.Pin_0, R8.Pin_0, R9.Pin_0, R10.Pin_0, R11.Pin_0, R12.Pin_0, R13.Pin_0, R14.Pin_0, R15.Pin_0, R16.Pin_0, R17.Pin_0, R19.Pin_0
  N11: IC1.GPB0, RE5.EncoderPinA, R9.Pin_1
  N12: IC1.GPB1, RE5.EncoderPinB, R10.Pin_1
  N13: IC1.GPB2, RE6.EncoderPinA, R11.Pin_1
  N14: IC1.GPB3, RE6.EncoderPinB, R12.Pin_1
  N15: IC1.GPB4, RE7.EncoderPinA, R13.Pin_1
  N16: IC1.GPB5, RE7.EncoderPinB, R14.Pin_1
  N17: IC1.GPB6, RE8.EncoderPinA, R15.Pin_1
  N18: IC1.GPB7, RE8.EncoderPinB, R16.Pin_1
  N19: IC1.GPA0, RE4.EncoderPinB, R8.Pin_1
  N20: IC1.GPA1, RE4.EncoderPinA, R7.Pin_1
  N21: IC1.GPA2, RE3.EncoderPinB, R6.Pin_1
  N22: IC1.GPA3, RE3.EncoderPinA, R5.Pin_1
  N23: IC1.GPA4, RE2.EncoderPinB, R4.Pin_1
  N24: IC1.GPA5, RE2.EncoderPinA, R3.Pin_1
  N25: IC1.GPA6, RE1.EncoderPinB, R2.Pin_1
  N26: IC1.GPA7, RE1.EncoderPinA, R1.Pin_1
  N27: S1.Pin_3, S1.Pin_4
  N28: S2.Pin_3, S2.Pin_4
  N29: S3.Pin_3, S3.Pin_4
  N30: S4.Pin_3, S4.Pin_4

custom parts:
  SparkFun Pro Micro: The Pro Micro is similar to the Pro Mini except with an ATmega32U4 on board. The USB transceiver inside the 32U4 allows us to add USB connectivity on-board and do away with bulky external USB interface. Based on: https://github.com/unorthodox-engineers/unorthodox-arduino/blob/master/Unorthodox/fritzing/parts/Pro%20Micro.fzpz
  MCP23017 I2C I/O Expander: The MCP23017 uses two i2c pins (these can be shared with other i2c devices), and in exchange gives you 16 general purpose pins. You can set each of 16 pins to be input, output, input with a pullup or open drain. There's even the ability to get an interrupt via an external pin when any of the inputs change so you don't have to keep polling the chip.
  Rotary Encoder with Knob: Rotary Encoder with 1/4" Shaft and Knob
  Pushbutton: A generic pushbutton. This is a standard 12mm square momentary button. What we really like is the large button head and good tactile feel (it ‘clicks’ really well). This button is great for user input on a PCB or a good, big reset button on a breadboard. Breadboard friendly! SparkFun Storefront SKU: COM-09190 Modified by: Ho Yun "Bobby" Chan @ SparkFun Electronics Inc.
