# Fritzing sketch usb-teensy3.6 (saved by Fritzing 0.9.4)
circuit board: 15cm x 9cm
perfboards: 1

parts:
  R3 = Slide Potentiometer [maximum_resistance=100kΩ]
  R1 = Slide Potentiometer [maximum_resistance=100kΩ]
  R2 = Slide Potentiometer [maximum_resistance=100kΩ]
  R6 = Rotary Potentiometer (Large) [maximum_resistance=100kΩ package=THT]
  R7 = Rotary Potentiometer (Large) [maximum_resistance=100kΩ package=THT]
  S1 = SWITCH-MOMENTARY-2 [package=tactile-pth-12mm]
  S2 = SWITCH-MOMENTARY-2 [package=tactile-pth-12mm]
  R8 = Rotary Potentiometer (Large) [maximum_resistance=100kΩ package=THT]
  R4 = Slide Potentiometer [maximum_resistance=100kΩ]
  R5 = Slide Potentiometer [maximum_resistance=100kΩ]
  R9 = Rotary Potentiometer (Large) [maximum_resistance=100kΩ package=THT]
  R10 = Rotary Potentiometer (Large) [maximum_resistance=100kΩ package=THT]
  Teensy_3_6 = Teensy 3.6 (Basic)

nets:
  N1: R3.leg1, R1.leg1, R2.leg1, R6.leg1, R7.leg1, R8.leg1, R4.leg1, R5.leg1, R9.leg1, R10.leg1, Teensy_3_6.Vin
  N2: R3.wiper, Teensy_3_6.A1/D15
  GND: R3.leg2, R1.leg2, R2.leg2, R6.leg2, R7.leg2, S1.2, S2.2, R8.leg2, R4.leg2, R5.leg2, R9.leg2, R10.leg2, Teensy_3_6.GND, Teensy_3_6.GND1
  N3: R1.wiper, Teensy_3_6.A3/D17
  N4: R2.wiper, Teensy_3_6.A2/D16
  N5: R6.wiper, Teensy_3_6.A4/D18
  N6: R7.wiper, Teensy_3_6.A5/D19
  N7: S1.1, Teensy_3_6.D39
  N8: S2.1, Teensy_3_6.A21/DAC0
  N9: R8.wiper, Teensy_3_6.A6/D20
  N10: R4.wiper, Teensy_3_6.A0/D14
  N11: R5.wiper, Teensy_3_6.A22/DAC1
  N12: R9.wiper, Teensy_3_6.A7/D21
  N13: R10.wiper, Teensy_3_6.A8/D22
  N14: Teensy_3_6.3V3, Teensy_3_6.3V3_1

notes:
  Just a little impression

custom parts:
  Teensy 3.6 (Basic): The Teensy is a complete USB-based microcontoller development system, in a very small footprint, capable of implementing many types of projects. All programming is done via the USB port. No special programmer is needed, only a standard micro-USB cable and a PC or Macintosh with a USB port.
