# Fritzing sketch themvp (saved by Fritzing 0.9.4)
perfboards: 1

parts:
  Teensy_LC1 = Teensy-LC
  RE3 = Rotary Encoder [part_number=RK09K package=THT]
  RE1 = Rotary Encoder [part_number=RK09K package=THT]
  RE2 = Rotary Encoder [part_number=RK09K package=THT]
  RE4 = Rotary Encoder [part_number=RK09K package=THT]
  RE5 = Rotary Encoder [part_number=RK09K package=THT]
  RE6 = Rotary Encoder [part_number=RK09K package=THT]
  RE7 = Rotary Encoder [part_number=RK09K package=THT]
  RE8 = Rotary Encoder [part_number=RK09K package=THT]
  S9 = Pushbutton [package="[THT]"]
  S10 = Pushbutton [package="[THT]"]
  S11 = Pushbutton [package="[THT]"]
  S12 = Pushbutton [package="[THT]"]
  S13 = Pushbutton [package="[THT]"]
  S14 = Pushbutton [package="[THT]"]
  S15 = Pushbutton [package="[THT]"]
  S16 = Pushbutton [package="[THT]"]
  S17 = Pushbutton [package="[THT]"]
  S18 = Pushbutton [package="[THT]"]
  S19 = Pushbutton [package="[THT]"]
  S20 = Pushbutton [package="[THT]"]
  S21 = Pushbutton [package="[THT]"]
  S22 = Pushbutton [package="[THT]"]
  R1 = Rotary Potentiometer (Small) [maximum_resistance=100kΩ package=THT]

nets:
  N1: Teensy_LC1.GND, Teensy_LC1.D4, Teensy_LC1.D7, Teensy_LC1.D10, S9.Pin_3, S9.Pin_4, S10.Pin_3, S10.Pin_4, S11.Pin_3, S11.Pin_4, S12.Pin_3, S12.Pin_4, S13.Pin_3, S13.Pin_4, S14.Pin_3, S14.Pin_4, S15.Pin_3, S15.Pin_4, S17.Pin_3, S17.Pin_4, S20.Pin_3, S20.Pin_4
  N2: Teensy_LC1.D12, Teensy_LC1.A0/D14, S16.Pin_3, S16.Pin_4, S19.Pin_3, S19.Pin_4, S22.Pin_3, S22.Pin_4
  N3: Teensy_LC1.A1/D15, R1.wiper
  N4: Teensy_LC1.A2/D16, RE5.EncoderPinC, S10.Pin_1, S10.Pin_2
  N5: Teensy_LC1.A3/D17, RE4.EncoderPinC
  N6: Teensy_LC1.A4/D18, RE6.EncoderPinC
  N7: Teensy_LC1.A5/D19, RE3.EncoderPinC
  N8: Teensy_LC1.A6/D20, RE7.EncoderPinC
  N9: Teensy_LC1.A7/D21, RE2.EncoderPinC
  N10: Teensy_LC1.A8/D22, RE8.EncoderPinC
  N11: Teensy_LC1.A9/D23, RE1.EncoderPinC
  N12: Teensy_LC1.3V3#30, RE3.EncoderPinA, RE1.EncoderPinA, RE2.EncoderPinA, RE4.EncoderPinA, RE5.EncoderPinA, RE6.EncoderPinA, RE7.EncoderPinA, RE8.EncoderPinA, R1.leg1
  N13: Teensy_LC1.AGND, RE3.EncoderPinB, RE1.EncoderPinB, RE2.EncoderPinB, RE4.EncoderPinB, RE5.EncoderPinB, RE6.EncoderPinB, RE7.EncoderPinB, RE8.EncoderPinB, S16.Pin_1, S16.Pin_2, R1.leg2
  N14: Teensy_LC1.A11, S13.Pin_1, S13.Pin_2
  N15: S9.Pin_1, S9.Pin_2
  N16: S14.Pin_1, S14.Pin_2
  N17: S15.Pin_1, S15.Pin_2
  N18: S17.Pin_1, S17.Pin_2
  N19: S18.Pin_1, S18.Pin_2
  N20: S18.Pin_3, S18.Pin_4, S21.Pin_3, S21.Pin_4
  N21: S19.Pin_1, S19.Pin_2
  N22: S20.Pin_1, S20.Pin_2
  N23: S21.Pin_1, S21.Pin_2
  N24: S22.Pin_1, S22.Pin_2

custom parts:
  Teensy-LC: Teensy-LC (Low Cost) is a powerful 32 bit microcontroller board, with a rich set of hardware peripherals, at a very affordable price! Teensy-LC delivers an impressive collection of capabilities to make modern electronic projects simpler. It features an ARM Cortex-M0+ processor at 48 MHz, 62K Flash, 8K RAM, 12 bit analog input & output, hardware Serial, SPI & I2C, USB, and a total of 27 I/O pins.
